// Logisim project branch-comp.circ as structural Verilog: 1 circuit, main circuit branch_comp
module branch_comp (
  input  [31:0] BrData1,
  input  [31:0] BrData2,
  input  BrUn,
  output BrEq,
  output BrLt
);

  wire BrEq_s, BrEq_u, BrLt_s, BrLt_u;

  Multiplexer multiplexer_1 (.in0(BrEq_s), .in1(BrEq_u), .out(BrEq), .sel(BrUn));
  Comparator #(.width(32)) comparator_1 (.a(BrData1), .b(BrData2), .eq(BrEq_s), .lt(BrLt_s));  // open: gt
  Comparator #(.mode("unsigned"), .width(32)) comparator_2 (
    .a(BrData1), .b(BrData2), .eq(BrEq_u), .lt(BrLt_u));  // open: gt
  Multiplexer multiplexer_2 (.in0(BrLt_s), .in1(BrLt_u), .out(BrLt), .sel(BrUn));

  // Notes on the sheet:
  //   INPUTS to your circuit
  //   DON'T CHANGE THE LOCATIONS OF THE INPUTS AND OUTPUTS!
  //   OUTPUT from your circuit
endmodule
