// Logisim project control-logic.circ as structural Verilog: 1 circuit, main circuit control_logic
module control_logic (
  input  [31:0] Instruction,
  input  BrEq,
  input  BrLt,
  output PCSel,
  output RegWEn,
  output [2:0] ImmSel,
  output BrUn,
  output ASel,
  output BSel,
  output [3:0] ALUSel,
  output MemWEn,
  output [1:0] WBSel
);

  wire and_21_out, and_22_out, and_23_out, and_24_out, comparator_1_eq, comparator_2_eq, comparator_3_eq,
       comparator_4_eq, comparator_5_eq, comparator_6_eq, comparator_7_eq, comparator_8_eq, comparator_9_eq,
       comparator_10_eq, comparator_11_eq, comparator_14_eq, comparator_15_eq, comparator_16_eq,
       comparator_17_eq, comparator_18_eq, comparator_19_eq, comparator_20_eq, comparator_21_eq,
       comparator_22_eq, comparator_23_eq, comparator_24_eq, comparator_25_eq, comparator_26_eq,
       comparator_27_eq, comparator_28_eq, comparator_29_eq, comparator_30_eq, comparator_31_eq,
       comparator_32_eq, comparator_33_eq, comparator_34_eq, comparator_35_eq, comparator_36_eq,
       comparator_37_eq, comparator_38_eq, comparator_39_eq, comparator_40_eq, comparator_41_eq,
       comparator_42_eq, comparator_43_eq, comparator_46_eq, comparator_47_eq, comparator_48_eq,
       comparator_49_eq, comparator_50_eq, comparator_51_eq, comparator_53_eq, comparator_54_eq, is_add,
       is_addi, is_and, is_andi, is_auipc, is_b, is_beq, is_bge, is_bgeu, is_blt, is_bltu, is_bne, is_i,
       is_jal, is_jalr, is_lb, is_lh, is_load, is_lui, is_lw, is_mul, is_mulh, is_mulhu, is_or, is_ori, is_r,
       is_sb, is_sh, is_sll, is_slli, is_slt, is_slti, is_sra, is_srai, is_srl, is_srli, is_store, is_sub,
       is_sw, is_xor, is_xori, not_1_out, not_2_out, or_1_out, or_2_out;
  wire [5:0] address;
  wire [15:14] rom_1_data;

  ROM #(.addrWidth(6), .dataWidth(16)) rom_1 (
    .addr(address), .data({rom_1_data, WBSel, ALUSel, MemWEn, BSel, ASel, BrUn, ImmSel, RegWEn}));
  Comparator #(.width(3)) comparator_1 (.a(Instruction[14:12]), .b(3'b000), .eq(comparator_1_eq));  // open: gt, lt
  Comparator #(.width(3)) comparator_2 (.a(Instruction[14:12]), .b(3'b111), .eq(comparator_2_eq));  // open: gt, lt
  Comparator #(.width(3)) comparator_3 (.a(Instruction[14:12]), .b(3'b110), .eq(comparator_3_eq));  // open: gt, lt
  Comparator #(.width(3)) comparator_4 (.a(Instruction[14:12]), .b(3'b100), .eq(comparator_4_eq));  // open: gt, lt
  Comparator #(.width(3)) comparator_5 (.a(Instruction[14:12]), .b(3'b001), .eq(comparator_5_eq));  // open: gt, lt
  Comparator #(.width(7)) comparator_6 (.a(Instruction[31:25]), .b({7{1'b0}}), .eq(comparator_6_eq));  // open: gt, lt
  Comparator #(.width(3)) comparator_7 (.a(Instruction[14:12]), .b(3'b101), .eq(comparator_7_eq));  // open: gt, lt
  Comparator #(.width(7)) comparator_8 (.a(Instruction[31:25]), .b({7{1'b0}}), .eq(comparator_8_eq));  // open: gt, lt
  Comparator #(.width(3)) comparator_9 (.a(Instruction[14:12]), .b(3'b101), .eq(comparator_9_eq));  // open: gt, lt
  Comparator #(.width(7)) comparator_10 (
    .a(Instruction[31:25]), .b(7'b0100000), .eq(comparator_10_eq));  // open: gt, lt
  Comparator #(.width(3)) comparator_11 (.a(Instruction[14:12]), .b(3'b010), .eq(comparator_11_eq));  // open: gt, lt
  Comparator #(.width(7)) comparator_12 (.a(Instruction[6:0]), .b(7'b0010011), .eq(is_i));  // open: gt, lt
  and and_1 (is_addi, is_i, comparator_1_eq);
  and and_2 (is_andi, is_i, comparator_2_eq);
  and and_3 (is_ori, is_i, comparator_3_eq);
  and and_4 (is_xori, is_i, comparator_4_eq);
  and and_5 (is_slli, is_i, comparator_5_eq, comparator_6_eq);
  and and_6 (is_srli, is_i, comparator_7_eq, comparator_8_eq);
  and and_7 (is_srai, is_i, comparator_9_eq, comparator_10_eq);
  and and_8 (is_slti, is_i, comparator_11_eq);
  Priority_Encoder #(.select_enc(6)) priority_encoder_1 (
    .in0(is_addi), .in1(is_andi), .in2(is_ori), .in3(is_xori), .in4(is_slli), .in5(is_srli), .in6(is_srai),
    .in7(is_slti), .in8(is_add), .in9(is_sub), .in10(is_and), .in11(is_or), .in12(is_xor), .in13(is_sll),
    .in14(is_srl), .in15(is_sra), .in16(is_slt), .in17(is_mul), .in18(is_mulh), .in19(is_mulhu),
    .in20(is_beq), .in21(is_bge), .in22(is_bgeu), .in23(is_blt), .in24(is_bltu), .in25(is_bne), .in26(is_lb),
    .in27(is_lh), .in28(is_lw), .in29(is_sb), .in30(is_sh), .in31(is_sw), .in32(is_jal), .in33(is_jalr),
    .in34(is_auipc), .in35(is_lui), .out(address));  // open: in36, in37, in38, in39, in40, in41, in42, in43, in44, in45, in46, in47, in48, in49, in50, in51, in52, in53, in54, in55, in56, in57, in58, in59, in60, in61, in62, in63, gs, en_out, en_in
  Comparator #(.width(7)) comparator_13 (.a(Instruction[6:0]), .b(7'b0110011), .eq(is_r));  // open: gt, lt
  Comparator #(.width(3)) comparator_14 (.a(Instruction[14:12]), .b(3'b000), .eq(comparator_14_eq));  // open: gt, lt
  Comparator #(.width(7)) comparator_15 (.a(Instruction[31:25]), .b({7{1'b0}}), .eq(comparator_15_eq));  // open: gt, lt
  Comparator #(.width(3)) comparator_16 (.a(Instruction[14:12]), .b(3'b000), .eq(comparator_16_eq));  // open: gt, lt
  Comparator #(.width(7)) comparator_17 (
    .a(Instruction[31:25]), .b(7'b0100000), .eq(comparator_17_eq));  // open: gt, lt
  Comparator #(.width(3)) comparator_18 (.a(Instruction[14:12]), .b(3'b111), .eq(comparator_18_eq));  // open: gt, lt
  Comparator #(.width(7)) comparator_19 (.a(Instruction[31:25]), .b({7{1'b0}}), .eq(comparator_19_eq));  // open: gt, lt
  Comparator #(.width(3)) comparator_20 (.a(Instruction[14:12]), .b(3'b110), .eq(comparator_20_eq));  // open: gt, lt
  Comparator #(.width(7)) comparator_21 (.a(Instruction[31:25]), .b({7{1'b0}}), .eq(comparator_21_eq));  // open: gt, lt
  Comparator #(.width(3)) comparator_22 (.a(Instruction[14:12]), .b(3'b100), .eq(comparator_22_eq));  // open: gt, lt
  Comparator #(.width(7)) comparator_23 (.a(Instruction[31:25]), .b({7{1'b0}}), .eq(comparator_23_eq));  // open: gt, lt
  Comparator #(.width(3)) comparator_24 (.a(Instruction[14:12]), .b(3'b001), .eq(comparator_24_eq));  // open: gt, lt
  Comparator #(.width(7)) comparator_25 (.a(Instruction[31:25]), .b({7{1'b0}}), .eq(comparator_25_eq));  // open: gt, lt
  Comparator #(.width(3)) comparator_26 (.a(Instruction[14:12]), .b(3'b101), .eq(comparator_26_eq));  // open: gt, lt
  Comparator #(.width(7)) comparator_27 (.a(Instruction[31:25]), .b({7{1'b0}}), .eq(comparator_27_eq));  // open: gt, lt
  Comparator #(.width(3)) comparator_28 (.a(Instruction[14:12]), .b(3'b101), .eq(comparator_28_eq));  // open: gt, lt
  Comparator #(.width(7)) comparator_29 (
    .a(Instruction[31:25]), .b(7'b0100000), .eq(comparator_29_eq));  // open: gt, lt
  Comparator #(.width(3)) comparator_30 (.a(Instruction[14:12]), .b(3'b010), .eq(comparator_30_eq));  // open: gt, lt
  Comparator #(.width(7)) comparator_31 (.a(Instruction[31:25]), .b({7{1'b0}}), .eq(comparator_31_eq));  // open: gt, lt
  Comparator #(.width(3)) comparator_32 (.a(Instruction[14:12]), .b(3'b000), .eq(comparator_32_eq));  // open: gt, lt
  Comparator #(.width(7)) comparator_33 (
    .a(Instruction[31:25]), .b(7'b0000001), .eq(comparator_33_eq));  // open: gt, lt
  Comparator #(.width(3)) comparator_34 (.a(Instruction[14:12]), .b(3'b001), .eq(comparator_34_eq));  // open: gt, lt
  Comparator #(.width(7)) comparator_35 (
    .a(Instruction[31:25]), .b(7'b0000001), .eq(comparator_35_eq));  // open: gt, lt
  Comparator #(.width(3)) comparator_36 (.a(Instruction[14:12]), .b(3'b011), .eq(comparator_36_eq));  // open: gt, lt
  Comparator #(.width(7)) comparator_37 (
    .a(Instruction[31:25]), .b(7'b0000001), .eq(comparator_37_eq));  // open: gt, lt
  and and_9 (is_add, is_r, comparator_14_eq, comparator_15_eq);
  and and_10 (is_sub, is_r, comparator_16_eq, comparator_17_eq);
  and and_11 (is_and, is_r, comparator_18_eq, comparator_19_eq);
  and and_12 (is_or, is_r, comparator_20_eq, comparator_21_eq);
  and and_13 (is_xor, is_r, comparator_22_eq, comparator_23_eq);
  and and_14 (is_sll, is_r, comparator_24_eq, comparator_25_eq);
  and and_15 (is_srl, is_r, comparator_26_eq, comparator_27_eq);
  and and_16 (is_sra, is_r, comparator_28_eq, comparator_29_eq);
  and and_17 (is_slt, is_r, comparator_30_eq, comparator_31_eq);
  and and_18 (is_mul, is_r, comparator_32_eq, comparator_33_eq);
  and and_19 (is_mulh, is_r, comparator_34_eq, comparator_35_eq);
  and and_20 (is_mulhu, is_r, comparator_36_eq, comparator_37_eq);
  or or_1 (or_1_out, is_blt, is_bltu);
  or or_2 (or_2_out, is_bge, is_bgeu);
  not not_1 (not_1_out, BrEq);
  not not_2 (not_2_out, BrLt);
  and and_21 (and_21_out, is_beq, BrEq);
  and and_22 (and_22_out, is_bne, not_1_out);
  and and_23 (and_23_out, or_1_out, BrLt);
  and and_24 (and_24_out, or_2_out, not_2_out);
  Comparator #(.width(3)) comparator_38 (.a(Instruction[14:12]), .b(3'b000), .eq(comparator_38_eq));  // open: gt, lt
  Comparator #(.width(3)) comparator_39 (.a(Instruction[14:12]), .b(3'b101), .eq(comparator_39_eq));  // open: gt, lt
  Comparator #(.width(3)) comparator_40 (.a(Instruction[14:12]), .b(3'b111), .eq(comparator_40_eq));  // open: gt, lt
  Comparator #(.width(3)) comparator_41 (.a(Instruction[14:12]), .b(3'b100), .eq(comparator_41_eq));  // open: gt, lt
  Comparator #(.width(3)) comparator_42 (.a(Instruction[14:12]), .b(3'b110), .eq(comparator_42_eq));  // open: gt, lt
  Comparator #(.width(3)) comparator_43 (.a(Instruction[14:12]), .b(3'b001), .eq(comparator_43_eq));  // open: gt, lt
  Comparator #(.width(7)) comparator_44 (.a(Instruction[6:0]), .b(7'b1100011), .eq(is_b));  // open: gt, lt
  and and_25 (is_beq, is_b, comparator_38_eq);
  and and_26 (is_bge, is_b, comparator_39_eq);
  and and_27 (is_bgeu, is_b, comparator_40_eq);
  and and_28 (is_blt, is_b, comparator_41_eq);
  and and_29 (is_bltu, is_b, comparator_42_eq);
  and and_30 (is_bne, is_b, comparator_43_eq);
  or or_3 (PCSel, is_jal, and_22_out, and_23_out, and_21_out, and_24_out, is_jalr);
  Comparator #(.width(7)) comparator_45 (.a(Instruction[6:0]), .b(7'b0000011), .eq(is_load));  // open: gt, lt
  Comparator #(.width(3)) comparator_46 (.a(Instruction[14:12]), .b(3'b000), .eq(comparator_46_eq));  // open: gt, lt
  Comparator #(.width(3)) comparator_47 (.a(Instruction[14:12]), .b(3'b001), .eq(comparator_47_eq));  // open: gt, lt
  Comparator #(.width(3)) comparator_48 (.a(Instruction[14:12]), .b(3'b010), .eq(comparator_48_eq));  // open: gt, lt
  Comparator #(.width(3)) comparator_49 (.a(Instruction[14:12]), .b(3'b000), .eq(comparator_49_eq));  // open: gt, lt
  Comparator #(.width(3)) comparator_50 (.a(Instruction[14:12]), .b(3'b001), .eq(comparator_50_eq));  // open: gt, lt
  Comparator #(.width(3)) comparator_51 (.a(Instruction[14:12]), .b(3'b010), .eq(comparator_51_eq));  // open: gt, lt
  and and_31 (is_lb, is_load, comparator_46_eq);
  and and_32 (is_lh, is_load, comparator_47_eq);
  and and_33 (is_lw, is_load, comparator_48_eq);
  Comparator #(.width(7)) comparator_52 (.a(Instruction[6:0]), .b(7'b0100011), .eq(is_store));  // open: gt, lt
  and and_34 (is_sb, is_store, comparator_49_eq);
  and and_35 (is_sh, is_store, comparator_50_eq);
  and and_36 (is_sw, is_store, comparator_51_eq);
  Comparator #(.width(7)) comparator_53 (.a(Instruction[6:0]), .b(7'b1100111), .eq(comparator_53_eq));  // open: gt, lt
  Comparator #(.width(3)) comparator_54 (.a(Instruction[14:12]), .b(3'b000), .eq(comparator_54_eq));  // open: gt, lt
  Comparator #(.width(7)) comparator_55 (.a(Instruction[6:0]), .b(7'b1101111), .eq(is_jal));  // open: gt, lt
  and and_37 (is_jalr, comparator_53_eq, comparator_54_eq);
  Comparator #(.width(7)) comparator_56 (.a(Instruction[6:0]), .b(7'b0010111), .eq(is_auipc));  // open: gt, lt
  Comparator #(.width(7)) comparator_57 (.a(Instruction[6:0]), .b(7'b0110111), .eq(is_lui));  // open: gt, lt

  // Other names for the same wires on the sheet: opcode[6:0] = Instruction[6:0]; rd[4:0] = Instruction[11:7];
  //   funct3[2:0] = Instruction[14:12]; rs1[4:0] = Instruction[19:15]; rs2[4:0] = Instruction[24:20];
  //   funct7[6:0] = Instruction[31:25]

  // Notes on the sheet:
  //   INPUTS to your circuit
  //   contents of rom_1 (hex, n*v repeats v):
  //   61 761 661 461 161 561 d61 261 21 c21 721 621 421 121 521 d21 221 821 921 b21 44 44 54 44 54 44 2061
  //   2061 2061 e2 e2 e2 1049 1061 47 f47
  //   ROM FOR CONTROL LOGIC
  //   DON'T CHANGE THE LOCATIONS OF THE INPUTS AND OUTPUTS!
  //   This is only if you choose to do the ROM option
  //   OUTPUT from your circuit
  //   Reminder: If using ROM, use combinational logic for PCSel
endmodule
