// Logisim project imm-gen.circ as structural Verilog: 1 circuit, main circuit imm_gen
module imm_gen (
  input  [31:0] Instruction,
  input  [2:0] ImmSel,
  output [31:0] Immediate
);

  wire [31:0] Immediate_i;
  wire [31:5] Immediate_s;
  wire [31:12] Immediate_b;
  wire [31:20] Immediate_j;

  assign Immediate_i = {{20{Instruction[31]}}, Instruction[31:20]};  // Bit_Extender bit_extender_1
  assign Immediate_s = {{20{Instruction[31]}}, Instruction[31:25]};  // Bit_Extender bit_extender_2
  assign Immediate_b = {{19{Instruction[31]}}, Instruction[31]};  // Bit_Extender bit_extender_3
  assign Immediate_j = {{11{Instruction[31]}}, Instruction[31]};  // Bit_Extender bit_extender_4
  Multiplexer #(.select(3), .width(32)) multiplexer_1 (
    .in0(Immediate_i), .in1({Immediate_s, Instruction[11:7]}),
    .in2({Immediate_b, Instruction[7], Instruction[30:25], Instruction[11:8], 1'b0}),
    .in3({Instruction[31:12], {12{1'b0}}}),
    .in4({Immediate_j, Instruction[19:12], Instruction[20], Instruction[30:21], 1'b0}), .out(Immediate),
    .sel(ImmSel));  // open: in5, in6, in7

  // Other names for the same wires on the sheet: Immediate_b[11:1] = {Instruction[7], Instruction[30:25], Instruction[11:8]};
  //   Immediate_s[4:0] = Instruction[11:7];
  //   Immediate_j[19:1] = {Instruction[19:12], Instruction[20], Instruction[30:21]};
  //   Immediate_u[31:12] = Instruction[31:12]

  // Notes on the sheet:
  //   INPUTS to your circuit
  //   DON'T CHANGE THE LOCATIONS OF THE INPUTS AND OUTPUTS!
  //   OUTPUT from your circuit
endmodule
