// Logisim project partial-store.circ as structural Verilog: 1 circuit, main circuit partial_store
module partial_store (
  input  [31:0] Instruction,
  input  [31:0] MemAddress,
  input  [31:0] DataFromReg,
  input  MemWEn,
  output [3:0] MemWriteMask,
  output [31:0] DataToMem
);

  wire [3:0] mask_sb, mask_sh, multiplexer_4_out;
  wire [4:0] bit_extender_1_out, shifter_1_out;
  wire [31:0] and_1_out, multiplexer_3_out, shifter_2_out;

  Multiplexer #(.select(2), .width(4)) multiplexer_1 (
    .in0(4'b0001), .in1(4'b0010), .in2(4'b0100), .in3(4'b1000), .out(mask_sb), .sel(MemAddress[1:0]));
  Multiplexer #(.select(2), .width(4)) multiplexer_2 (
    .in0(4'b0011), .in2(4'b1100), .out(mask_sh), .sel(MemAddress[1:0]));  // open: in1, in3
  Multiplexer #(.select(3), .width(32)) multiplexer_3 (
    .in0(32'hff), .in1(32'hffff), .in2({32{1'b1}}), .out(multiplexer_3_out), .sel(Instruction[14:12]));  // open: in3, in4, in5, in6, in7
  assign bit_extender_1_out = {{3{MemAddress[1]}}, MemAddress[1:0]};  // Bit_Extender bit_extender_1
  assign and_1_out = multiplexer_3_out & DataFromReg;  // AND_Gate and_1, 32 bits wide
  Shifter #(.width(5)) shifter_1 (.in(bit_extender_1_out), .\dist (3'b011), .out(shifter_1_out));
  Multiplexer #(.select(3), .width(4)) multiplexer_4 (
    .in0(mask_sb), .in1(mask_sh), .in2(4'b1111), .out(multiplexer_4_out), .sel(Instruction[14:12]));  // open: in3, in4, in5, in6, in7
  Shifter #(.width(32)) shifter_2 (.in(and_1_out), .\dist (shifter_1_out), .out(shifter_2_out));
  Multiplexer #(.width(4)) multiplexer_5 (.in0(4'b0000), .in1(multiplexer_4_out), .out(MemWriteMask), .sel(MemWEn));
  Multiplexer #(.width(32)) multiplexer_6 (.in0({32{1'b0}}), .in1(shifter_2_out), .out(DataToMem), .sel(MemWEn));

  // Other names for the same wires on the sheet: funct3[2:0] = Instruction[14:12]; offset[1:0] = MemAddress[1:0]

  // Notes on the sheet:
  //   INPUTS to your circuit
  //   DON'T CHANGE THE LOCATIONS OF THE INPUTS AND OUTPUTS!
  //   OUTPUT from your circuit
endmodule
