// Logisim project regfile.circ as structural Verilog: 1 circuit, main circuit regfile
module regfile (
  input  [4:0] ReadIndex1,
  input  [4:0] ReadIndex2,
  input  [4:0] WriteIndex,
  input  [31:0] WriteData,
  input  RegWEn,
  input  clk,
  output [31:0] ra,
  output [31:0] sp,
  output [31:0] t0,
  output [31:0] t1,
  output [31:0] t2,
  output [31:0] s0,
  output [31:0] s1,
  output [31:0] a0,
  output [31:0] ReadData1,
  output [31:0] ReadData2
);

  wire and_1_out, and_2_out, and_3_out, and_4_out, and_5_out, and_6_out, and_7_out, and_8_out, and_9_out,
       and_10_out, and_11_out, and_12_out, and_13_out, and_14_out, and_15_out, and_16_out, and_17_out,
       and_18_out, and_19_out, and_20_out, and_21_out, and_22_out, and_23_out, and_24_out, and_25_out,
       and_26_out, and_27_out, and_28_out, and_29_out, and_30_out, and_31_out, we0, we1, we2, we3, we4, we5,
       we6, we7, we8, we9, we10, we11, we12, we13, we14, we15, we16, we17, we18, we19, we20, we21, we22,
       we23, we24, we25, we26, we27, we28, we29, we30, we31;
  wire [31:0] x0, x3, x4, x11, x12, x13, x14, x15, x16, x17, x18, x19, x20, x21, x22, x23, x24, x25, x26,
       x27, x28, x29, x30, x31;

  Decoder #(.enable("false"), .select(5)) decoder_1 (
    .out0(we0), .out1(we1), .out2(we2), .out3(we3), .out4(we4), .out5(we5), .out6(we6), .out7(we7),
    .out8(we8), .out9(we9), .out10(we10), .out11(we11), .out12(we12), .out13(we13), .out14(we14),
    .out15(we15), .out16(we16), .out17(we17), .out18(we18), .out19(we19), .out20(we20), .out21(we21),
    .out22(we22), .out23(we23), .out24(we24), .out25(we25), .out26(we26), .out27(we27), .out28(we28),
    .out29(we29), .out30(we30), .out31(we31), .sel(WriteIndex));
  and and_1 (and_1_out, we1, RegWEn);
  and and_2 (and_2_out, we2, RegWEn);
  and and_3 (and_3_out, we3, RegWEn);
  and and_4 (and_4_out, we4, RegWEn);
  and and_5 (and_5_out, we5, RegWEn);
  and and_6 (and_6_out, we6, RegWEn);
  and and_7 (and_7_out, we7, RegWEn);
  and and_8 (and_8_out, we8, RegWEn);
  and and_9 (and_9_out, we9, RegWEn);
  and and_10 (and_10_out, we10, RegWEn);
  and and_11 (and_11_out, we11, RegWEn);
  and and_12 (and_12_out, we12, RegWEn);
  and and_13 (and_13_out, we13, RegWEn);
  and and_14 (and_14_out, we14, RegWEn);
  and and_15 (and_15_out, we15, RegWEn);
  Register #(.width(32)) register_1 (.D(WriteData), .en(1'b0), .clk(clk), .Q(x0));  // open: clr
  Register #(.width(32)) register_2 (.D(WriteData), .en(and_1_out), .clk(clk), .Q(ra));  // open: clr
  Register #(.width(32)) register_3 (.D(WriteData), .en(and_2_out), .clk(clk), .Q(sp));  // open: clr
  Register #(.width(32)) register_4 (.D(WriteData), .en(and_3_out), .clk(clk), .Q(x3));  // open: clr
  Register #(.width(32)) register_5 (.D(WriteData), .en(and_4_out), .clk(clk), .Q(x4));  // open: clr
  Register #(.width(32)) register_6 (.D(WriteData), .en(and_5_out), .clk(clk), .Q(t0));  // open: clr
  Register #(.width(32)) register_7 (.D(WriteData), .en(and_6_out), .clk(clk), .Q(t1));  // open: clr
  Register #(.width(32)) register_8 (.D(WriteData), .en(and_8_out), .clk(clk), .Q(s0));  // open: clr
  Register #(.width(32)) register_9 (.D(WriteData), .en(and_7_out), .clk(clk), .Q(t2));  // open: clr
  Register #(.width(32)) register_10 (.D(WriteData), .en(and_9_out), .clk(clk), .Q(s1));  // open: clr
  Register #(.width(32)) register_11 (.D(WriteData), .en(and_10_out), .clk(clk), .Q(a0));  // open: clr
  Register #(.width(32)) register_12 (.D(WriteData), .en(and_11_out), .clk(clk), .Q(x11));  // open: clr
  Register #(.width(32)) register_13 (.D(WriteData), .en(and_12_out), .clk(clk), .Q(x12));  // open: clr
  Register #(.width(32)) register_14 (.D(WriteData), .en(and_13_out), .clk(clk), .Q(x13));  // open: clr
  Register #(.width(32)) register_15 (.D(WriteData), .en(and_14_out), .clk(clk), .Q(x14));  // open: clr
  Register #(.width(32)) register_16 (.D(WriteData), .en(and_15_out), .clk(clk), .Q(x15));  // open: clr
  and and_16 (and_16_out, we16, RegWEn);
  and and_17 (and_17_out, we17, RegWEn);
  and and_18 (and_18_out, we18, RegWEn);
  and and_19 (and_19_out, we19, RegWEn);
  and and_20 (and_20_out, we20, RegWEn);
  and and_21 (and_21_out, we21, RegWEn);
  and and_22 (and_22_out, we22, RegWEn);
  and and_23 (and_23_out, we23, RegWEn);
  and and_24 (and_24_out, we24, RegWEn);
  and and_25 (and_25_out, we25, RegWEn);
  and and_26 (and_26_out, we26, RegWEn);
  and and_27 (and_27_out, we27, RegWEn);
  and and_28 (and_28_out, we28, RegWEn);
  and and_29 (and_29_out, we29, RegWEn);
  and and_30 (and_30_out, we30, RegWEn);
  and and_31 (and_31_out, we31, RegWEn);
  Register #(.width(32)) register_17 (.D(WriteData), .en(and_16_out), .clk(clk), .Q(x16));  // open: clr
  Register #(.width(32)) register_18 (.D(WriteData), .en(and_17_out), .clk(clk), .Q(x17));  // open: clr
  Register #(.width(32)) register_19 (.D(WriteData), .en(and_18_out), .clk(clk), .Q(x18));  // open: clr
  Register #(.width(32)) register_20 (.D(WriteData), .en(and_19_out), .clk(clk), .Q(x19));  // open: clr
  Register #(.width(32)) register_21 (.D(WriteData), .en(and_20_out), .clk(clk), .Q(x20));  // open: clr
  Register #(.width(32)) register_22 (.D(WriteData), .en(and_21_out), .clk(clk), .Q(x21));  // open: clr
  Register #(.width(32)) register_23 (.D(WriteData), .en(and_22_out), .clk(clk), .Q(x22));  // open: clr
  Register #(.width(32)) register_24 (.D(WriteData), .en(and_23_out), .clk(clk), .Q(x23));  // open: clr
  Register #(.width(32)) register_25 (.D(WriteData), .en(and_24_out), .clk(clk), .Q(x24));  // open: clr
  Register #(.width(32)) register_26 (.D(WriteData), .en(and_25_out), .clk(clk), .Q(x25));  // open: clr
  Register #(.width(32)) register_27 (.D(WriteData), .en(and_26_out), .clk(clk), .Q(x26));  // open: clr
  Register #(.width(32)) register_28 (.D(WriteData), .en(and_27_out), .clk(clk), .Q(x27));  // open: clr
  Register #(.width(32)) register_29 (.D(WriteData), .en(and_28_out), .clk(clk), .Q(x28));  // open: clr
  Register #(.width(32)) register_30 (.D(WriteData), .en(and_29_out), .clk(clk), .Q(x29));  // open: clr
  Register #(.width(32)) register_31 (.D(WriteData), .en(and_30_out), .clk(clk), .Q(x30));  // open: clr
  Register #(.width(32)) register_32 (.D(WriteData), .en(and_31_out), .clk(clk), .Q(x31));  // open: clr
  Multiplexer #(.select(5), .width(32)) multiplexer_1 (
    .in0(x0), .in1(ra), .in2(sp), .in3(x3), .in4(x4), .in5(t0), .in6(t1), .in7(t2), .in8(s0), .in9(s1),
    .in10(a0), .in11(x11), .in12(x12), .in13(x13), .in14(x14), .in15(x15), .in16(x16), .in17(x17),
    .in18(x18), .in19(x19), .in20(x20), .in21(x21), .in22(x22), .in23(x23), .in24(x24), .in25(x25),
    .in26(x26), .in27(x27), .in28(x28), .in29(x29), .in30(x30), .in31(x31), .out(ReadData1), .sel(ReadIndex1));
  Multiplexer #(.select(5), .width(32)) multiplexer_2 (
    .in0(x0), .in1(ra), .in2(sp), .in3(x3), .in4(x4), .in5(t0), .in6(t1), .in7(t2), .in8(s0), .in9(s1),
    .in10(a0), .in11(x11), .in12(x12), .in13(x13), .in14(x14), .in15(x15), .in16(x16), .in17(x17),
    .in18(x18), .in19(x19), .in20(x20), .in21(x21), .in22(x22), .in23(x23), .in24(x24), .in25(x25),
    .in26(x26), .in27(x27), .in28(x28), .in29(x29), .in30(x30), .in31(x31), .out(ReadData2), .sel(ReadIndex2));

  // Other names for the same wires on the sheet: x1[31:0] = ra; x2[31:0] = sp; x5[31:0] = t0; x6[31:0] = t1;
  //   x7[31:0] = t2; x8[31:0] = s0; x9[31:0] = s1; x10[31:0] = a0

  // Notes on the sheet:
  //   INPUTS to your circuit
  //   DON'T CHANGE THE LOCATIONS OF THE INPUTS AND OUTPUTS!
  //   These are DEBUG/TEST outputs from your circuit.
  //   OUTPUTS from your circuit
endmodule
